// Logisim project 1112.circ as structural Verilog: 3 circuits, main circuit main
module main (
  input  [7:0] in_1,
  input  [7:0] in_2,
  input  in_3,
  input  [7:0] yuan,
  output [7:0] bu
);

  wire clock_1_out;
  wire [3:0] mul_1_count;
  wire [7:0] mul_1_product;

  buma buma_1 (.in_1(yuan), .out_2(bu));
  Clock clock_1 (.out(clock_1_out));
  mul mul_1 (
    .muit_op1(in_1), .muit_op2(in_2), .reset(in_3), .clk(clock_1_out), .product(mul_1_product),
    .count(mul_1_count));
  Hex_Digit_Display hex_digit_display_1 (.value(mul_1_count));  // open: dp
  Hex_Digit_Display hex_digit_display_2 (.value(mul_1_product[7:4]));  // open: dp
  Hex_Digit_Display hex_digit_display_3 (.value(mul_1_product[3:0]));  // open: dp
endmodule

module buma (
  input  [7:0] in_1,
  output [7:0] out_2
);

  wire not_1_out;
  wire [6:0] negator_1_out;

  Negator #(.width(7)) negator_1 (.in(in_1[6:0]), .out(negator_1_out));
  assign out_2 = not_1_out ? in_1 : 8'bz;  // Controlled_Buffer controlled_buffer_1
  not not_1 (not_1_out, in_1[7]);
  assign out_2 = in_1[7] ? {in_1[7], negator_1_out} : 8'bz;  // Controlled_Buffer controlled_buffer_2

  // Other names for the same wires on the sheet: fuhao = in_1[7]
endmodule

module mul (
  input  [7:0] muit_op1,
  input  [7:0] muit_op2,
  input  reset,
  input  clk,
  output [7:0] product,
  output [3:0] count
);

  wire and_1_out, counter_2_carry, not_1_out;
  wire [0:0] x_q;
  wire [6:0] multiplexer_1_out, multiplexer_2_out, multiplexer_6_out, negator_1_out, negator_2_out,
       negator_3_out, x_q_2;
  wire [7:0] adder_1_out, bei_q, ji_q, multiplexer_3_out, multiplexer_4_out, multiplexer_5_out;
  wire [7:7] xor_1_out;

  not not_1 (not_1_out, reset);
  // NAND_Gate nand_1 is placed but not wired
  xor xor_1 (xor_1_out[7], muit_op1[7], muit_op2[7]);
  Negator #(.width(7)) negator_1 (.in(muit_op1[6:0]), .out(negator_1_out));
  Negator #(.width(7)) negator_2 (.in(muit_op2[6:0]), .out(negator_2_out));
  and and_1 (and_1_out, not_1_out, counter_2_carry);
  BitSelector bitselector_1 ();  // open: in, out, sel
  Multiplexer #(.width(7)) multiplexer_1 (
    .in0(muit_op1[6:0]), .in1(negator_1_out), .out(multiplexer_1_out), .sel(muit_op1[7]));
  Multiplexer #(.width(7)) multiplexer_2 (
    .in0(muit_op2[6:0]), .in1(negator_2_out), .out(multiplexer_2_out), .sel(muit_op2[7]));
  Demultiplexer demultiplexer_1 ();  // open: out0, out1, in, sel
  Decoder decoder_1 ();  // open: out0, out1, sel, en
  Register bei (.D({1'b0, multiplexer_1_out}), .en(1'b1), .clk(clk), .Q(bei_q));  // open: clr
  Multiplexer #(.width(8)) multiplexer_3 (.in0({8{1'b0}}), .in1(bei_q), .out(multiplexer_3_out), .sel(x_q_2[6]));
  Adder adder_1 (.a(ji_q), .b(multiplexer_3_out), .out(adder_1_out));  // open: cin, cout
  Counter #(.max('hf), .width(4)) counter_1 ();  // open: clr, load, up, count, clk, D, carry, Q
  Register x (.D(multiplexer_4_out), .en(1'b1), .clk(clk), .Q({x_q_2, x_q[0]}));  // open: clr
  Multiplexer #(.width(8)) multiplexer_4 (
    .in0({adder_1_out[0], x_q_2[5:0], x_q[0]}), .in1({1'b0, multiplexer_2_out}), .out(multiplexer_4_out),
    .sel(reset));
  Register ji (.D(multiplexer_5_out), .en(1'b1), .clk(clk), .Q(ji_q));  // open: clr
  Multiplexer #(.width(8)) multiplexer_5 (
    .in0({adder_1_out[7:1], 1'b0}), .in1({8{1'b0}}), .out(multiplexer_5_out), .sel(reset));
  Counter #(.max('hf), .width(4)) counter_2 (
    .clr(1'b0), .load(reset), .up(1'b0), .count(1'b1), .clk(clk), .D(4'b0000), .carry(counter_2_carry),
    .Q(count));
  Negator #(.width(7)) negator_3 (.in(x_q_2), .out(negator_3_out));
  Multiplexer #(.width(7)) multiplexer_6 (
    .in0(x_q_2), .in1(negator_3_out), .out(multiplexer_6_out), .sel(xor_1_out[7]));
  Multiplexer #(.width(8)) multiplexer_7 (
    .in0({xor_1_out[7], multiplexer_6_out}), .in1({8{1'b1}}), .out(product), .sel(and_1_out));
endmodule
