// Logisim project 2.5new.circ as structural Verilog: 3 circuits, main circuit main
module main (
  input  [19:0] address,
  input  BHE,
  input  WR,
  input  RD,
  input  A0,
  output out_6,
  output out_7,
  output out_8,
  output out_9,
  output out_10,
  output out_11,
  output out_12,
  output out_13,
  output out_14,
  output out_15,
  output out_16,
  output out_17,
  output out_18,
  output out_19,
  output out_20,
  output out_21
);

  wire and_1_out, and_2_out, and_3_out, and_4_out, clock_1_out, clock_2_out, clock_3_out, EN, hefa, ji,
       not_1_out, not_2_out, not_3_out, not_4_out, not_5_out, not_6_out, not_7_out, not_8_out, or_1_out,
       or_2_out, or_3_out, or_4_out, or_5_out, or_6_out, or_7_out, or_8_out, ou, word;
  wire [7:0] controlled_buffer_1_out, controlled_buffer_3_out, RAMji, RAMou, ROMji, ROMou;
  wire [15:0] controlled_buffer_5_out, controlled_buffer_6_out, controlled_buffer_7_out,
       controlled_buffer_8_out, dizhi_1_as;

  not not_1 (not_1_out, EN);
  assign controlled_buffer_1_out = EN ? RAMou : 8'bz;  // Controlled_Buffer controlled_buffer_1
  assign controlled_buffer_1_out = not_1_out ? ROMji : 8'bz;  // Controlled_Buffer controlled_buffer_2
  assign controlled_buffer_3_out = EN ? RAMji : 8'bz;  // Controlled_Buffer controlled_buffer_3
  assign controlled_buffer_3_out = not_2_out ? ROMou : 8'bz;  // Controlled_Buffer controlled_buffer_4
  not not_2 (not_2_out, EN);
  dizhi dizhi_1 (.address(address), .as(dizhi_1_as), .deng(hefa), .EN(EN));
  BHE_AD bhe_ad_1 (.BHE(BHE), .A0(A0), .WORD(word), .OU(ou), .JI(ji));
  or or_1 (or_1_out, word, ji);
  or or_2 (or_2_out, word, ou);
  not not_3 (not_3_out, or_1_out);
  not not_4 (not_4_out, or_2_out);
  or or_3 (or_3_out, not_3_out, hefa);
  or or_4 (or_4_out, not_4_out, hefa);
  Clock clock_1 (.out(clock_1_out));
  D_Flip_Flop d_ff_1 (
    .D(controlled_buffer_1_out[7]), .clk(clock_1_out), .Q(out_6), .reset(or_4_out));  // open: Qn, preset
  D_Flip_Flop d_ff_2 (
    .D(controlled_buffer_1_out[6]), .clk(clock_1_out), .Q(out_7), .reset(or_4_out));  // open: Qn, preset
  D_Flip_Flop d_ff_3 (
    .D(controlled_buffer_1_out[5]), .clk(clock_1_out), .Q(out_8), .reset(or_4_out));  // open: Qn, preset
  D_Flip_Flop d_ff_4 (
    .D(controlled_buffer_1_out[4]), .clk(clock_1_out), .Q(out_9), .reset(or_4_out));  // open: Qn, preset
  D_Flip_Flop d_ff_5 (
    .D(controlled_buffer_1_out[3]), .clk(clock_1_out), .Q(out_10), .reset(or_4_out));  // open: Qn, preset
  D_Flip_Flop d_ff_6 (
    .D(controlled_buffer_1_out[2]), .clk(clock_1_out), .Q(out_11), .reset(or_4_out));  // open: Qn, preset
  D_Flip_Flop d_ff_7 (
    .D(controlled_buffer_1_out[1]), .clk(clock_1_out), .Q(out_12), .reset(or_4_out));  // open: Qn, preset
  D_Flip_Flop d_ff_8 (
    .D(controlled_buffer_1_out[0]), .clk(clock_1_out), .Q(out_13), .reset(or_4_out));  // open: Qn, preset
  D_Flip_Flop d_ff_9 (
    .D(controlled_buffer_3_out[7]), .clk(clock_1_out), .Q(out_14), .reset(or_3_out));  // open: Qn, preset
  D_Flip_Flop d_ff_10 (
    .D(controlled_buffer_3_out[6]), .clk(clock_1_out), .Q(out_15), .reset(or_3_out));  // open: Qn, preset
  D_Flip_Flop d_ff_11 (
    .D(controlled_buffer_3_out[5]), .clk(clock_1_out), .Q(out_16), .reset(or_3_out));  // open: Qn, preset
  D_Flip_Flop d_ff_12 (
    .D(controlled_buffer_3_out[4]), .clk(clock_1_out), .Q(out_17), .reset(or_3_out));  // open: Qn, preset
  D_Flip_Flop d_ff_13 (
    .D(controlled_buffer_3_out[3]), .clk(clock_1_out), .Q(out_18), .reset(or_3_out));  // open: Qn, preset
  D_Flip_Flop d_ff_14 (
    .D(controlled_buffer_3_out[2]), .clk(clock_1_out), .Q(out_19), .reset(or_3_out));  // open: Qn, preset
  D_Flip_Flop d_ff_15 (
    .D(controlled_buffer_3_out[1]), .clk(clock_1_out), .Q(out_20), .reset(or_3_out));  // open: Qn, preset
  D_Flip_Flop d_ff_16 (
    .D(controlled_buffer_3_out[0]), .clk(clock_1_out), .Q(out_21), .reset(or_3_out));  // open: Qn, preset
  LED panduan (.in(hefa));
  not not_5 (not_5_out, EN);
  not not_6 (not_6_out, WR);
  not not_7 (not_7_out, RD);
  or or_5 (or_5_out, ji, word);
  or or_6 (or_6_out, ou, word);
  or or_7 (or_7_out, ji, word);
  not not_8 (not_8_out, EN);
  and and_1 (and_1_out, EN, or_5_out);
  and and_2 (and_2_out, EN, or_6_out);
  and and_3 (and_3_out, or_7_out, not_5_out);
  or or_8 (or_8_out, ou, word);
  Clock clock_2 (.out(clock_2_out));
  Clock clock_3 (.out(clock_3_out));
  and and_4 (and_4_out, or_8_out, not_8_out);
  RAM #(.addrWidth(16)) RAM_EVEN (
    .addr(controlled_buffer_5_out), .we(not_6_out), .oe(not_7_out), .clk(clock_2_out), .dout(RAMji));  // open: din
  assign controlled_buffer_5_out = and_1_out ? dizhi_1_as : 16'bz;  // Controlled_Buffer controlled_buffer_5
  RAM #(.addrWidth(16)) RAM_ODD (
    .addr(controlled_buffer_6_out), .we(not_6_out), .oe(not_7_out), .clk(clock_3_out), .dout(RAMou));  // open: din
  assign controlled_buffer_6_out = and_2_out ? dizhi_1_as : 16'bz;  // Controlled_Buffer controlled_buffer_6
  ROM #(.addrWidth(16)) ROM_EVEN (.addr(controlled_buffer_7_out), .data(ROMou));
  assign controlled_buffer_7_out = and_3_out ? dizhi_1_as : 16'bz;  // Controlled_Buffer controlled_buffer_7
  ROM #(.addrWidth(16)) ROM_ODD (.addr(controlled_buffer_8_out), .data(ROMji));
  assign controlled_buffer_8_out = and_4_out ? dizhi_1_as : 16'bz;  // Controlled_Buffer controlled_buffer_8

  // Notes on the sheet:
  //   contents of ROM_EVEN (hex, n*v repeats v):
  //   11 1 0 1 1 0 1 1 0 0 0 1 1
  //   contents of ROM_ODD (hex, n*v repeats v):
  //   12 7*10 0 1 0 1 0 1 0 1
endmodule

module dizhi (
  input  [19:0] address,
  output [15:0] as,
  output deng,
  output EN
);

  wire not_1_out, not_2_out, not_3_out, not_4_out, not_5_out;

  not not_1 (not_1_out, address[17]);
  not not_2 (not_2_out, address[18]);
  or or_1 (deng, not_1_out, not_2_out, not_3_out);
  not not_3 (not_3_out, address[19]);
  not not_4 (not_4_out, address[16]);
  not not_5 (not_5_out, deng);
  and and_1 (EN, not_4_out, not_5_out);

  assign as = address[15:0];
endmodule

module BHE_AD (
  input  BHE,
  input  A0,
  output WORD,
  output OU,
  output JI
);

  wire not_1_out, not_2_out;

  not not_1 (not_1_out, BHE);
  not not_2 (not_2_out, A0);
  and and_1 (WORD, not_2_out, not_1_out);
  and and_2 (OU, not_1_out, A0);
  and and_3 (JI, BHE, not_2_out);
endmodule
