// Logisim project 2_4new.circ as structural Verilog: 4 circuits, main circuit main
module shixian (
  input  [7:0] mult_op1,
  input  [7:0] mult_op2,
  input  rst,
  input  clk,
  output [7:0] product1,
  output [3:0] count9
);

  wire fuhao, start, stop;
  wire [6:0] multiplexer_3_out, negator_1_out, Y_q;
  wire [7:0] adder_1_cout, buma_1_out_2, buma_2_out_2, ji_q, multiplexer_1_out, multiplexer_2_out;
  wire [7:6] adder_1_out;

  xor xor_1 (fuhao, buma_1_out_2[7], buma_2_out_2[7]);
  buma buma_1 (.in_1(mult_op1), .out_2(buma_1_out_2));
  buma buma_2 (.in_1(mult_op2), .out_2(buma_2_out_2));
  Register ji (.D(adder_1_cout), .en(stop), .clk(clk), .Q(ji_q), .clr(rst));
  Multiplexer #(.width(8)) multiplexer_1 (
    .in0({8{1'b0}}), .in1({1'b0, buma_1_out_2[6:0]}), .out(multiplexer_1_out), .sel(Y_q[0]));
  Adder adder_1 (
    .a(ji_q), .b(multiplexer_1_out), .out({adder_1_cout[6:0], adder_1_out[7]}), .cout(adder_1_cout[7]));  // open: cin
  Register Y (.D(multiplexer_2_out), .en(stop), .clk(clk), .Q({adder_1_out[6], Y_q}), .clr(rst));
  Multiplexer #(.width(8)) multiplexer_2 (
    .in0({adder_1_out, Y_q[6:1]}), .in1({1'b0, buma_2_out_2[6:0]}), .out(multiplexer_2_out), .sel(start));
  Negator #(.width(7)) negator_1 (.in(Y_q), .out(negator_1_out));
  Counter #(.max('h9), .ongoal("stay"), .width(4)) counter_1 (
    .Q(count9), .clk(clk), .clr(rst));  // open: load, D, count, carry, up
  Comparator #(.mode("unsigned"), .width(4)) comparator_1 (.a(count9), .b(4'b0000), .eq(start));  // open: gt, lt
  Comparator #(.mode("unsigned"), .width(4)) comparator_2 (.a(count9), .b(4'b1001), .lt(stop));  // open: gt, eq
  Multiplexer #(.width(7)) multiplexer_3 (.in0(Y_q), .in1(negator_1_out), .out(multiplexer_3_out), .sel(fuhao));
  Multiplexer #(.width(8)) multiplexer_4 (
    .in0({fuhao, multiplexer_3_out}), .in1({8{1'b1}}), .out(product1), .sel(stop));
endmodule

module main (
  input  [7:0] yuan,
  input  [7:0] in_2,
  input  [7:0] in_3,
  input  in_4,
  input  [7:0] in_5,
  input  [7:0] in_6,
  input  in_7,
  input  [7:0] in_8,
  input  [7:0] in_9,
  input  in_10,
  input  [7:0] in_11,
  input  [7:0] in_12,
  input  in_13,
  input  [7:0] in_14,
  input  [7:0] in_15,
  input  in_16,
  output [7:0] bu
);

  wire clock_1_out, clock_2_out, clock_3_out, clock_4_out, clock_5_out;
  wire [3:0] shixian_1_count9, shixian_2_count9, shixian_3_count9, shixian_4_count9, shixian_5_count9;
  wire [7:0] shixian_1_product1, shixian_2_product1, shixian_3_product1, shixian_4_product1,
       shixian_5_product1;

  Clock clock_1 (.out(clock_1_out));
  Clock clock_2 (.out(clock_2_out));
  Clock clock_3 (.out(clock_3_out));
  Clock clock_4 (.out(clock_4_out));
  Clock clock_5 (.out(clock_5_out));
  shixian shixian_1 (
    .mult_op1(in_2), .mult_op2(in_3), .rst(in_4), .clk(clock_1_out), .product1(shixian_1_product1),
    .count9(shixian_1_count9));
  shixian shixian_2 (
    .mult_op1(in_5), .mult_op2(in_6), .rst(in_7), .clk(clock_2_out), .product1(shixian_2_product1),
    .count9(shixian_2_count9));
  shixian shixian_3 (
    .mult_op1(in_8), .mult_op2(in_9), .rst(in_10), .clk(clock_3_out), .product1(shixian_3_product1),
    .count9(shixian_3_count9));
  shixian shixian_4 (
    .mult_op1(in_11), .mult_op2(in_12), .rst(in_13), .clk(clock_4_out), .product1(shixian_4_product1),
    .count9(shixian_4_count9));
  shixian shixian_5 (
    .mult_op1(in_14), .mult_op2(in_15), .rst(in_16), .clk(clock_5_out), .product1(shixian_5_product1),
    .count9(shixian_5_count9));
  Hex_Digit_Display hex_digit_display_1 (.value(shixian_1_count9));  // open: dp
  Hex_Digit_Display hex_digit_display_2 (.value(shixian_2_count9));  // open: dp
  Hex_Digit_Display hex_digit_display_3 (.value(shixian_3_count9));  // open: dp
  Hex_Digit_Display hex_digit_display_4 (.value(shixian_4_count9));  // open: dp
  Hex_Digit_Display hex_digit_display_5 (.value(shixian_5_count9));  // open: dp
  Hex_Digit_Display hex_digit_display_6 (.value(shixian_1_product1[7:4]));  // open: dp
  Hex_Digit_Display hex_digit_display_7 (.value(shixian_2_product1[7:4]));  // open: dp
  Hex_Digit_Display hex_digit_display_8 (.value(shixian_3_product1[7:4]));  // open: dp
  Hex_Digit_Display hex_digit_display_9 (.value(shixian_4_product1[7:4]));  // open: dp
  Hex_Digit_Display hex_digit_display_10 (.value(shixian_5_product1[7:4]));  // open: dp
  Hex_Digit_Display hex_digit_display_11 (.value(shixian_1_product1[3:0]));  // open: dp
  Hex_Digit_Display hex_digit_display_12 (.value(shixian_2_product1[3:0]));  // open: dp
  Hex_Digit_Display hex_digit_display_13 (.value(shixian_3_product1[3:0]));  // open: dp
  Hex_Digit_Display hex_digit_display_14 (.value(shixian_4_product1[3:0]));  // open: dp
  Hex_Digit_Display hex_digit_display_15 (.value(shixian_5_product1[3:0]));  // open: dp
  buma buma_1 (.in_1(yuan), .out_2(bu));
endmodule

module buma (
  input  [7:0] in_1,
  output [7:0] out_2
);

  wire not_1_out;
  wire [6:0] negator_1_out;

  Negator #(.width(7)) negator_1 (.in(in_1[6:0]), .out(negator_1_out));
  assign out_2 = not_1_out ? in_1 : 8'bz;  // Controlled_Buffer controlled_buffer_1
  not not_1 (not_1_out, in_1[7]);
  assign out_2 = in_1[7] ? {in_1[7], negator_1_out} : 8'bz;  // Controlled_Buffer controlled_buffer_2

  // Other names for the same wires on the sheet: fuhao = in_1[7]
endmodule

module mul (
  input  [7:0] muit_op1,
  input  [7:0] muit_op2,
  input  reset,
  input  clk,
  output [7:0] product,
  output [3:0] count
);

  wire and_1_out, counter_2_carry, not_1_out, undriven;
  wire [0:0] x_q;
  wire [6:0] multiplexer_1_out, multiplexer_2_out, multiplexer_6_out, negator_1_out, negator_2_out,
       negator_3_out, x_q_2;
  wire [7:0] adder_1_out, bei_q, ji_q, multiplexer_3_out, multiplexer_4_out, multiplexer_5_out;
  wire [7:7] xor_1_out;

  not not_1 (not_1_out, reset);
  // NAND_Gate nand_1 is placed but not wired
  xor xor_1 (xor_1_out[7], muit_op1[7], muit_op2[7]);
  Negator #(.width(7)) negator_1 (.in(muit_op1[6:0]), .out(negator_1_out));
  Negator #(.width(7)) negator_2 (.in(muit_op2[6:0]), .out(negator_2_out));
  and and_1 (and_1_out, not_1_out, counter_2_carry);
  BitSelector bitselector_1 ();  // open: in, out, sel
  Multiplexer #(.width(7)) multiplexer_1 (
    .in0(muit_op1[6:0]), .in1(negator_1_out), .out(multiplexer_1_out), .sel(muit_op1[7]));
  Multiplexer #(.width(7)) multiplexer_2 (
    .in0(muit_op2[6:0]), .in1(negator_2_out), .out(multiplexer_2_out), .sel(muit_op2[7]));
  Demultiplexer demultiplexer_1 ();  // open: out0, out1, in, sel
  Decoder decoder_1 ();  // open: out0, out1, sel, en
  Register bei (.D({1'b0, multiplexer_1_out}), .en(1'b1), .clk(undriven), .Q(bei_q));  // open: clr
  Multiplexer #(.width(8)) multiplexer_3 (.in0({8{1'b0}}), .in1(bei_q), .out(multiplexer_3_out), .sel(x_q_2[6]));
  Adder adder_1 (.a(ji_q), .b(multiplexer_3_out), .out(adder_1_out));  // open: cin, cout
  Counter #(.max('hf), .width(4)) counter_1 ();  // open: clr, load, up, count, clk, D, carry, Q
  Register x (.D(multiplexer_4_out), .en(1'b1), .clk(undriven), .Q({x_q_2, x_q[0]}));  // open: clr
  Multiplexer #(.width(8)) multiplexer_4 (
    .in0({adder_1_out[0], x_q_2[5:0], x_q[0]}), .in1({1'b0, multiplexer_2_out}), .out(multiplexer_4_out),
    .sel(reset));
  Register ji (.D(multiplexer_5_out), .en(1'b1), .clk(undriven), .Q(ji_q));  // open: clr
  Multiplexer #(.width(8)) multiplexer_5 (
    .in0({adder_1_out[7:1], 1'b0}), .in1({8{1'b0}}), .out(multiplexer_5_out), .sel(reset));
  Counter #(.max('hf), .width(4)) counter_2 (
    .clr(1'b0), .load(reset), .up(1'b0), .count(1'b1), .clk(undriven), .D(4'b0000), .carry(counter_2_carry),
    .Q(count));
  Negator #(.width(7)) negator_3 (.in(x_q_2), .out(negator_3_out));
  Multiplexer #(.width(7)) multiplexer_6 (
    .in0(x_q_2), .in1(negator_3_out), .out(multiplexer_6_out), .sel(xor_1_out[7]));
  Multiplexer #(.width(8)) multiplexer_7 (
    .in0({xor_1_out[7], multiplexer_6_out}), .in1({8{1'b1}}), .out(product), .sel(and_1_out));
endmodule
