// Logisim project 3.2.circ as structural Verilog: 2 circuits, main circuit eightPart
module eightPart (
  input  A3,
  input  A4,
  input  A5,
  input  wen,
  input  [31:0] wdata,
  input  clk,
  input  A0,
  input  A1,
  input  A2,
  input  [2:0] waddr,
  output [31:0] cout2,
  output [31:0] cout
);

  wire and_1_out, and_2_out, and_3_out, and_4_out, and_5_out, and_6_out, and_7_out, and_8_out, and_9_out,
       and_10_out, and_11_out, and_12_out, and_13_out, and_14_out, and_15_out, and_16_out, n74138_1_pin4,
       n74138_1_pin6, n74138_1_pin7, n74138_1_pin9, n74138_1_pin10, n74138_1_pin11, n74138_1_pin12,
       n74138_1_pin13, n74138_1_pin14, n74138_1_pin15, n74138_2_pin4, n74138_2_pin6, n74138_2_pin7,
       n74138_2_pin9, n74138_2_pin10, n74138_2_pin11, n74138_2_pin12, n74138_2_pin13, n74138_2_pin14,
       n74138_2_pin15, n74138_3_pin4, n74138_3_pin6, n74138_3_pin7, n74138_3_pin9, n74138_3_pin10,
       n74138_3_pin11, n74138_3_pin12, n74138_3_pin13, n74138_3_pin14, n74138_3_pin15, not_1_out, not_2_out,
       not_3_out, not_4_out, not_5_out, not_6_out, not_7_out, not_8_out, not_9_out, not_18_out, not_19_out,
       not_20_out, not_21_out, not_22_out, not_23_out, not_24_out, not_25_out, w0, w1, w2, w3, w4, w5, w6, w7;
  wire [31:0] register_1_q, register_2_q, register_3_q, register_4_q, register_5_q, register_6_q,
       register_7_q, register_8_q;

  _74138 u_74138_1 (
    .pin1(A0), .pin2(A1), .pin3(A2), .pin4(n74138_1_pin4), .pin5(n74138_1_pin4), .pin6(n74138_1_pin6),
    .pin7(n74138_1_pin7), .pin15(n74138_1_pin15), .pin14(n74138_1_pin14), .pin13(n74138_1_pin13),
    .pin12(n74138_1_pin12), .pin11(n74138_1_pin11), .pin10(n74138_1_pin10), .pin9(n74138_1_pin9));
  _74138 u_74138_2 (
    .pin1(waddr[0]), .pin2(waddr[1]), .pin3(waddr[2]), .pin4(n74138_2_pin4), .pin5(n74138_2_pin4),
    .pin6(n74138_2_pin6), .pin7(n74138_2_pin7), .pin15(n74138_2_pin15), .pin14(n74138_2_pin14),
    .pin13(n74138_2_pin13), .pin12(n74138_2_pin12), .pin11(n74138_2_pin11), .pin10(n74138_2_pin10),
    .pin9(n74138_2_pin9));
  not not_1 (not_1_out, wen);
  not not_2 (not_2_out, n74138_1_pin15);
  not not_3 (not_3_out, n74138_1_pin14);
  not not_4 (not_4_out, n74138_1_pin13);
  not not_5 (not_5_out, n74138_1_pin12);
  not not_6 (not_6_out, n74138_1_pin11);
  not not_7 (not_7_out, n74138_1_pin10);
  not not_8 (not_8_out, n74138_1_pin9);
  not not_9 (not_9_out, n74138_1_pin7);
  not not_10 (w0, n74138_2_pin15);
  not not_11 (w1, n74138_2_pin14);
  not not_12 (w2, n74138_2_pin13);
  not not_13 (w3, n74138_2_pin12);
  not not_14 (w4, n74138_2_pin11);
  not not_15 (w5, n74138_2_pin10);
  not not_16 (w6, n74138_2_pin9);
  not not_17 (w7, n74138_2_pin7);
  and and_1 (and_1_out, not_1_out, not_2_out);
  and and_2 (and_2_out, not_1_out, not_3_out);
  and and_3 (and_3_out, not_1_out, not_4_out);
  and and_4 (and_4_out, not_1_out, not_5_out);
  and and_5 (and_5_out, not_1_out, not_6_out);
  and and_6 (and_6_out, not_1_out, not_7_out);
  and and_7 (and_7_out, not_1_out, not_8_out);
  and and_8 (and_8_out, not_1_out, not_9_out);
  Register #(.width(32)) register_1 (.D(wdata), .en(and_9_out), .clk(clk), .Q(register_1_q));  // open: clr
  and and_9 (and_9_out, w0, wen);
  Register #(.width(32)) register_2 (.D(wdata), .en(and_10_out), .clk(clk), .Q(register_2_q));  // open: clr
  and and_10 (and_10_out, w1, wen);
  Register #(.width(32)) register_3 (.D(wdata), .en(and_11_out), .clk(clk), .Q(register_3_q));  // open: clr
  and and_11 (and_11_out, w2, wen);
  Register #(.width(32)) register_4 (.D(wdata), .en(and_12_out), .clk(clk), .Q(register_4_q));  // open: clr
  and and_12 (and_12_out, w3, wen);
  Register #(.width(32)) register_5 (.D(wdata), .en(and_13_out), .clk(clk), .Q(register_5_q));  // open: clr
  and and_13 (and_13_out, w4, wen);
  Register #(.width(32)) register_6 (.D(wdata), .en(and_14_out), .clk(clk), .Q(register_6_q));  // open: clr
  and and_14 (and_14_out, w5, wen);
  Register #(.width(32)) register_7 (.D(wdata), .en(and_15_out), .clk(clk), .Q(register_7_q));  // open: clr
  and and_15 (and_15_out, w6, wen);
  Register #(.width(32)) register_8 (.D(wdata), .en(and_16_out), .clk(clk), .Q(register_8_q));  // open: clr
  and and_16 (and_16_out, w7, wen);
  assign cout = and_1_out ? register_1_q : 32'bz;  // Controlled_Buffer controlled_buffer_1
  assign cout = and_2_out ? register_2_q : 32'bz;  // Controlled_Buffer controlled_buffer_2
  assign cout = and_3_out ? register_3_q : 32'bz;  // Controlled_Buffer controlled_buffer_3
  assign cout = and_4_out ? register_4_q : 32'bz;  // Controlled_Buffer controlled_buffer_4
  assign cout = and_5_out ? register_5_q : 32'bz;  // Controlled_Buffer controlled_buffer_5
  assign cout = and_6_out ? register_6_q : 32'bz;  // Controlled_Buffer controlled_buffer_6
  assign cout = and_7_out ? register_7_q : 32'bz;  // Controlled_Buffer controlled_buffer_7
  assign cout = and_8_out ? register_8_q : 32'bz;  // Controlled_Buffer controlled_buffer_8
  _74138 u_74138_3 (
    .pin1(A3), .pin2(A4), .pin3(A5), .pin4(n74138_3_pin4), .pin5(n74138_3_pin4), .pin6(n74138_3_pin6),
    .pin7(n74138_3_pin7), .pin15(n74138_3_pin15), .pin14(n74138_3_pin14), .pin13(n74138_3_pin13),
    .pin12(n74138_3_pin12), .pin11(n74138_3_pin11), .pin10(n74138_3_pin10), .pin9(n74138_3_pin9));
  not not_18 (not_18_out, n74138_3_pin15);
  not not_19 (not_19_out, n74138_3_pin14);
  not not_20 (not_20_out, n74138_3_pin13);
  not not_21 (not_21_out, n74138_3_pin12);
  not not_22 (not_22_out, n74138_3_pin11);
  not not_23 (not_23_out, n74138_3_pin10);
  not not_24 (not_24_out, n74138_3_pin9);
  not not_25 (not_25_out, n74138_3_pin7);
  assign cout2 = not_18_out ? register_1_q : 32'bz;  // Controlled_Buffer controlled_buffer_9
  assign cout2 = not_19_out ? register_2_q : 32'bz;  // Controlled_Buffer controlled_buffer_10
  assign cout2 = not_20_out ? register_3_q : 32'bz;  // Controlled_Buffer controlled_buffer_11
  assign cout2 = not_21_out ? register_4_q : 32'bz;  // Controlled_Buffer controlled_buffer_12
  assign cout2 = not_22_out ? register_5_q : 32'bz;  // Controlled_Buffer controlled_buffer_13
  assign cout2 = not_23_out ? register_6_q : 32'bz;  // Controlled_Buffer controlled_buffer_14
  assign cout2 = not_24_out ? register_7_q : 32'bz;  // Controlled_Buffer controlled_buffer_15
  assign cout2 = not_25_out ? register_8_q : 32'bz;  // Controlled_Buffer controlled_buffer_16
  // also tied to GND on the sheet: {n74138_1_pin4, n74138_2_pin4, n74138_3_pin4}
  // also tied to VCC on the sheet: {n74138_1_pin6, n74138_2_pin6, n74138_3_pin6}
endmodule

module regfile (
  input  wen,
  input  [4:0] raddr2,
  input  [4:0] raddr1,
  input  [4:0] waddr,
  input  [31:0] wdata,
  output [31:0] rdata1,
  output [31:0] rdata2
);

  wire clock_1_out, n74139_1_pin1, n74139_1_pin4, n74139_1_pin5, n74139_1_pin6, n74139_1_pin7, n74139_1_pin9,
       n74139_1_pin10, n74139_1_pin11, n74139_1_pin12, n74139_2_pin4, n74139_2_pin5, n74139_2_pin6,
       n74139_2_pin7, w1, w2, w3, w4;
  wire [2:0] controlled_buffer_1_out, controlled_buffer_2_out, controlled_buffer_3_out,
       controlled_buffer_4_out;
  wire [3:0] not_1_out, not_4_out;
  wire [31:0] eightpart_1_cout, eightpart_1_cout2, eightpart_2_cout, eightpart_2_cout2, eightpart_3_cout,
       eightpart_3_cout2, eightpart_4_cout, eightpart_4_cout2;

  Clock clock_1 (.out(clock_1_out));
  _74139 u_74139_1 (
    .pin1(n74139_1_pin1), .pin2(raddr1[4]), .pin3(raddr1[3]), .pin4(n74139_1_pin4), .pin5(n74139_1_pin5),
    .pin6(n74139_1_pin6), .pin7(n74139_1_pin7), .pin15(n74139_1_pin1), .pin14(raddr2[4]), .pin13(raddr2[3]),
    .pin12(n74139_1_pin12), .pin11(n74139_1_pin11), .pin10(n74139_1_pin10), .pin9(n74139_1_pin9));
  _74139 u_74139_2 (
    .pin1(n74139_1_pin1), .pin2(waddr[3]), .pin3(waddr[4]), .pin4(n74139_2_pin4), .pin5(n74139_2_pin5),
    .pin6(n74139_2_pin6), .pin7(n74139_2_pin7));  // open: pin15, pin14, pin13, pin12, pin11, pin10, pin9
  not not_1 (not_1_out[0], n74139_1_pin12);
  not not_2 (not_1_out[2], n74139_1_pin11);
  not not_3 (not_1_out[1], n74139_1_pin10);
  not not_4 (not_4_out[0], n74139_1_pin4);
  not not_5 (not_4_out[2], n74139_1_pin5);
  not not_6 (not_4_out[1], n74139_1_pin6);
  not not_7 (not_4_out[3], n74139_1_pin7);
  not not_8 (w1, n74139_2_pin4);
  not not_9 (w3, n74139_2_pin5);
  not not_10 (w2, n74139_2_pin6);
  not not_11 (w4, n74139_2_pin7);
  not not_12 (not_1_out[3], n74139_1_pin9);
  assign controlled_buffer_1_out = w1 ? waddr[2:0] : 3'bz;  // Controlled_Buffer controlled_buffer_1
  assign controlled_buffer_2_out = w2 ? waddr[2:0] : 3'bz;  // Controlled_Buffer controlled_buffer_2
  assign controlled_buffer_3_out = w3 ? waddr[2:0] : 3'bz;  // Controlled_Buffer controlled_buffer_3
  assign controlled_buffer_4_out = w4 ? waddr[2:0] : 3'bz;  // Controlled_Buffer controlled_buffer_4
  eightPart eightpart_1 (
    .A3(raddr2[0]), .A4(raddr2[1]), .A5(raddr2[2]), .wen(wen), .wdata(wdata), .clk(clock_1_out),
    .A0(raddr1[0]), .A1(raddr1[1]), .A2(raddr1[2]), .waddr(controlled_buffer_1_out),
    .cout2(eightpart_1_cout2), .cout(eightpart_1_cout));
  eightPart eightpart_2 (
    .A3(raddr2[0]), .A4(raddr2[1]), .A5(raddr2[2]), .wen(wen), .wdata(wdata), .clk(clock_1_out),
    .A0(raddr1[0]), .A1(raddr1[1]), .A2(raddr1[2]), .waddr(controlled_buffer_2_out),
    .cout2(eightpart_2_cout2), .cout(eightpart_2_cout));
  eightPart eightpart_3 (
    .A3(raddr2[0]), .A4(raddr2[1]), .A5(raddr2[2]), .wen(wen), .wdata(wdata), .clk(clock_1_out),
    .A0(raddr1[0]), .A1(raddr1[1]), .A2(raddr1[2]), .waddr(controlled_buffer_3_out),
    .cout2(eightpart_3_cout2), .cout(eightpart_3_cout));
  eightPart eightpart_4 (
    .A3(raddr2[0]), .A4(raddr2[1]), .A5(raddr2[2]), .wen(wen), .wdata(wdata), .clk(clock_1_out),
    .A0(raddr1[0]), .A1(raddr1[1]), .A2(raddr1[2]), .waddr(controlled_buffer_4_out),
    .cout2(eightpart_4_cout2), .cout(eightpart_4_cout));
  Multiplexer #(.select(4), .width(32)) multiplexer_1 (
    .in1(eightpart_1_cout), .in2(eightpart_2_cout), .in4(eightpart_3_cout), .in8(eightpart_4_cout),
    .out(rdata1), .sel(not_4_out));  // open: in0, in3, in5, in6, in7, in9, in10, in11, in12, in13, in14, in15
  Multiplexer #(.select(4), .width(32)) multiplexer_2 (
    .in1(eightpart_1_cout2), .in2(eightpart_2_cout2), .in4(eightpart_3_cout2), .in8(eightpart_4_cout2),
    .out(rdata2), .sel(not_1_out));  // open: in0, in3, in5, in6, in7, in9, in10, in11, in12, in13, in14, in15
  // also tied to GND on the sheet: n74139_1_pin1

  // Other names for the same wires on the sheet: du1[2:0] = raddr1[2:0]; du2[2:0] = raddr2[2:0];
  //   wad[2:0] = waddr[2:0]
endmodule
