// Logisim project 3.4.circ as structural Verilog: 3 circuits, main circuit CU
module CU (
  input  [5:0] opcode,
  output RegDst,
  output RegWrite,
  output ALUSrc,
  output PCSrc,
  output MemRead,
  output MemWrite,
  output MemtoReg,
  output [2:0] ALUop
);

  wire and_2_out, and_3_out, and_7_out, not_1_out, not_2_out, not_3_out, not_4_out;

  not not_1 (not_1_out, opcode[5]);
  not not_2 (not_2_out, opcode[3]);
  not not_3 (not_3_out, opcode[2]);
  not not_4 (not_4_out, opcode[1]);
  not not_5 (RegDst, opcode[0]);
  and and_1 (ALUop[2], opcode[0], opcode[1], opcode[2]);
  and and_2 (and_2_out, not_2_out, not_3_out);
  and and_3 (and_3_out, not_1_out, opcode[3]);
  or or_1 (ALUSrc, opcode[3], opcode[1]);
  and and_4 (PCSrc, not_2_out, opcode[2]);
  and and_5 (MemRead, not_2_out, opcode[1]);
  and and_6 (MemWrite, opcode[3], not_3_out);
  and and_7 (and_7_out, opcode[3], not_4_out);
  and and_8 (ALUop[0], not_2_out, not_4_out);
  or or_2 (RegWrite, and_2_out, and_3_out);
  or or_3 (ALUop[1], and_7_out, RegDst);

  assign MemtoReg = opcode[5];
endmodule

module aluctrl (
  input  [5:0] alu_function,
  input  [2:0] aluop,
  output [4:0] alu_code
);

  wire and_1_out, and_2_out, and_3_out, not_1_out, not_2_out, not_3_out, not_4_out, not_5_out, not_6_out,
       not_7_out, not_8_out;
  wire [4:0] and_8_out;

  not not_1 (not_1_out, alu_function[2]);
  not not_2 (not_2_out, alu_function[3]);
  not not_3 (not_3_out, alu_function[4]);
  not not_4 (not_4_out, aluop[1]);
  not not_5 (not_5_out, aluop[0]);
  not not_6 (not_6_out, alu_function[1]);
  not not_7 (not_7_out, alu_function[0]);
  and and_1 (and_1_out, not_1_out, not_2_out, not_3_out, alu_function[5]);
  and and_2 (and_2_out, aluop[1], aluop[0], not_7_out);
  and and_3 (and_3_out, aluop[1], aluop[0], not_6_out);
  and and_4 (and_8_out[4], not_4_out, not_5_out);
  and and_5 (and_8_out[3], not_4_out, aluop[0]);
  and and_6 (and_8_out[2], and_1_out, and_2_out);
  and and_7 (and_8_out[1], and_1_out, and_3_out);
  and and_8 (and_8_out[0], aluop[1], not_5_out);
  assign alu_code = not_8_out ? and_8_out : 5'bz;  // Controlled_Buffer controlled_buffer_1
  not not_8 (not_8_out, aluop[2]);
endmodule

module cuAndalu (
  input  [5:0] in_1,
  input  [5:0] opcode,
  output [4:0] out_3
);

  wire [2:0] cu_1_aluop;

  CU cu_1 (.opcode(opcode), .ALUop(cu_1_aluop));  // open: RegDst, RegWrite, ALUSrc, PCSrc, MemRead, MemWrite, MemtoReg
  aluctrl aluctrl_1 (.alu_function(in_1), .aluop(cu_1_aluop), .alu_code(out_3));
endmodule
