// Logisim project cpuX.circ as structural Verilog: 18 circuits, main circuit main
module main (
  input  CLK,
  input  clr
);

  wire alu_1_zero, ALUSrc, and_1_out, Branch, clock_1_out, MemRead, MemtoReg, MemWrite, RegDst, Regwrite,
       SeSZ;
  wire [2:0] ALUop;
  wire [3:0] alucontrol_1_out_3;
  wire [4:0] multiplexer_1_out;
  wire [5:0] opcode;
  wire [25:0] rom_1_data;
  wire [31:0] adder_1_out, adder_2_out, alu_1_alu_result, firreg_1_rdata1, firreg_1_rdata2,
       multiplexer_2_out, multiplexer_3_out, multiplexer_4_out, multiplexer_5_out, pc_1_out_4, ram_1_dout,
       shifter_1_out, signextend_1_out_2, zeroextend_1_out_2;

  Clock clock_1 (.out(clock_1_out));
  ROM #(.dataWidth(32)) rom_1 (.addr(pc_1_out_4[9:2]), .data({opcode, rom_1_data}));
  PC pc_1 (.zero(clr), .CLK(clock_1_out), .in_3(multiplexer_4_out), .out_4(pc_1_out_4));
  cu cu_1 (
    .opcode(opcode), .ALUop(ALUop), .RegDst(RegDst), .RegWrite(Regwrite), .ALUSrc(ALUSrc), .MemRead(MemRead),
    .MemWrite(MemWrite), .MemtoReg(MemtoReg), .SeSZ(SeSZ), .Branch(Branch));
  Multiplexer #(.width(5)) multiplexer_1 (
    .in0(rom_1_data[20:16]), .in1(rom_1_data[15:11]), .out(multiplexer_1_out), .sel(RegDst));
  FirReg firreg_1 (
    .raddr1(rom_1_data[25:21]), .raddr2(rom_1_data[20:16]), .wen(Regwrite), .waddr(multiplexer_1_out),
    .wdata(multiplexer_5_out), .clk(clock_1_out), .rdata1(firreg_1_rdata1), .rdata2(firreg_1_rdata2));  // open: clr
  SignExtend signextend_1 (.in_1(rom_1_data[15:0]), .out_2(signextend_1_out_2));
  ZeroExtend zeroextend_1 (.in_1(rom_1_data[15:0]), .out_2(zeroextend_1_out_2));
  Adder #(.width(32)) adder_1 (.a(32'h4), .b(pc_1_out_4), .out(adder_1_out));  // open: cin, cout
  Shifter #(.width(32)) shifter_1 (.in(signextend_1_out_2), .\dist (5'b00010), .out(shifter_1_out));
  Multiplexer #(.width(32)) multiplexer_2 (
    .in0(firreg_1_rdata2), .in1(multiplexer_3_out), .out(multiplexer_2_out), .sel(ALUSrc));
  Multiplexer #(.width(32)) multiplexer_3 (
    .in0(signextend_1_out_2), .in1(zeroextend_1_out_2), .out(multiplexer_3_out), .sel(SeSZ));
  Adder #(.width(32)) adder_2 (.a(adder_1_out), .b(shifter_1_out), .out(adder_2_out));  // open: cin, cout
  ALU alu_1 (
    .alu_source1(firreg_1_rdata1), .alu_source2(multiplexer_2_out), .alu_control(alucontrol_1_out_3),
    .zero(alu_1_zero), .alu_result(alu_1_alu_result));
  alucontrol alucontrol_1 (.ALUop(ALUop), .func(rom_1_data[5:0]), .out_3(alucontrol_1_out_3));
  Multiplexer #(.width(32)) multiplexer_4 (
    .in0(adder_1_out), .in1(adder_2_out), .out(multiplexer_4_out), .sel(and_1_out));
  and and_1 (and_1_out, Branch, ~alu_1_zero);  // AND_Gate
  RAM #(.addrWidth(16), .asyncread("true"), .dataWidth(32)) ram_1 (
    .addr(alu_1_alu_result[17:2]), .we(MemWrite), .oe(MemRead), .clk(clock_1_out), .din(firreg_1_rdata2),
    .dout(ram_1_dout));
  Multiplexer #(.width(32)) multiplexer_5 (
    .in0(alu_1_alu_result), .in1(ram_1_dout), .out(multiplexer_5_out), .sel(MemtoReg));

  // Notes on the sheet:
  //   contents of rom_1 (hex, n*v repeats v):
  //   34080001 34090001 34110004 340c0100 3c040000 8c6821 1095021 35280000 35490000 ac890000 8c8b0000
  //   152b0004 34000000 912021 148dfff7 34000000 1620ffff 34000000
endmodule

module alucontrol (
  input  [2:0] ALUop,
  input  [5:0] func,
  output [3:0] out_3
);

  wire and_1_out, demultiplexer_1_out1, demultiplexer_1_out2, demultiplexer_1_out3, demultiplexer_1_out4;
  wire [3:0] multiplexer_1_out, multiplexer_2_out, multiplexer_3_out, multiplexer_4_out;

  Demultiplexer #(.select(3)) demultiplexer_1 (
    .out1(demultiplexer_1_out1), .out2(demultiplexer_1_out2), .out3(demultiplexer_1_out3),
    .out4(demultiplexer_1_out4), .in(1'b1), .sel(ALUop));  // open: out0, out5, out6, out7
  and and_1 (and_1_out, demultiplexer_1_out4, ~func[0]);  // AND_Gate
  Multiplexer #(.width(4)) multiplexer_1 (
    .in0(4'b0000), .in1(4'b0001), .out(multiplexer_1_out), .sel(demultiplexer_1_out1));
  Multiplexer #(.width(4)) multiplexer_2 (
    .in0(4'b0000), .in1(4'b0011), .out(multiplexer_2_out), .sel(demultiplexer_1_out2));
  Multiplexer #(.width(4)) multiplexer_3 (
    .in0(4'b0000), .in1(4'b0010), .out(multiplexer_3_out), .sel(demultiplexer_1_out3));
  Multiplexer #(.width(4)) multiplexer_4 (.in0(4'b0000), .in1(4'b0001), .out(multiplexer_4_out), .sel(and_1_out));
  assign out_3 = multiplexer_1_out | multiplexer_2_out | multiplexer_3_out | multiplexer_4_out;  // OR_Gate or_1, 4 bits wide
endmodule

module cu (
  input  [5:0] opcode,
  output [2:0] ALUop,
  output RegDst,
  output RegWrite,
  output ALUSrc,
  output MemRead,
  output MemWrite,
  output MemtoReg,
  output SeSZ,
  output Branch
);

  wire demultiplexer_1_out0, demultiplexer_1_out3, demultiplexer_1_out5, demultiplexer_1_out7,
       demultiplexer_2_out0, demultiplexer_2_out1, demultiplexer_2_out4, demultiplexer_2_out5, lui_out,
       ori_out;
  wire [2:0] multiplexer_1_out, multiplexer_2_out, multiplexer_3_out, multiplexer_4_out, multiplexer_5_out,
       multiplexer_6_out;

  Demultiplexer #(.select(3)) demultiplexer_1 (
    .out0(demultiplexer_1_out0), .out3(demultiplexer_1_out3), .out5(demultiplexer_1_out5),
    .out7(demultiplexer_1_out7), .in(1'b1), .sel(opcode[2:0]));  // open: out1, out2, out4, out6
  Demultiplexer #(.select(3)) demultiplexer_2 (
    .out0(demultiplexer_2_out0), .out1(demultiplexer_2_out1), .out4(demultiplexer_2_out4),
    .out5(demultiplexer_2_out5), .in(1'b1), .sel(opcode[5:3]));  // open: out2, out3, out6, out7
  and R (RegDst, demultiplexer_1_out0, demultiplexer_2_out0);
  and ori (ori_out, demultiplexer_1_out5, demultiplexer_2_out1);
  and lui (lui_out, demultiplexer_1_out7, demultiplexer_2_out1);
  and bne (Branch, demultiplexer_2_out0, demultiplexer_1_out5);
  and lw (MemRead, demultiplexer_2_out4, demultiplexer_1_out3);
  and sw (MemWrite, demultiplexer_1_out3, demultiplexer_2_out5);
  Multiplexer #(.width(3)) multiplexer_1 (.in0(3'b000), .in1(3'b100), .out(multiplexer_1_out), .sel(RegDst));
  Multiplexer #(.width(3)) multiplexer_2 (.in0(3'b000), .in1(3'b011), .out(multiplexer_2_out), .sel(ori_out));
  Multiplexer #(.width(3)) multiplexer_3 (.in0(3'b000), .in1(3'b010), .out(multiplexer_3_out), .sel(lui_out));
  Multiplexer #(.width(3)) multiplexer_4 (.in0(3'b000), .in1(3'b001), .out(multiplexer_4_out), .sel(Branch));
  Multiplexer #(.width(3)) multiplexer_5 (.in0(3'b000), .in1(3'b000), .out(multiplexer_5_out), .sel(MemRead));
  Multiplexer #(.width(3)) multiplexer_6 (.in0(3'b000), .in1(3'b000), .out(multiplexer_6_out), .sel(MemWrite));
  or or_1 (RegWrite, RegDst, ori_out, lui_out, MemRead);
  or or_2 (ALUSrc, ori_out, MemRead, MemWrite, lui_out);
  or or_3 (SeSZ, ori_out, lui_out);
  assign ALUop = multiplexer_1_out | multiplexer_2_out | multiplexer_3_out | multiplexer_4_out | multiplexer_5_out | multiplexer_6_out;  // OR_Gate or_4, 3 bits wide

  assign MemtoReg = MemRead;
endmodule

module FirReg (
  input  [4:0] raddr1,
  input  [4:0] raddr2,
  input  wen,
  input  [4:0] waddr,
  input  [31:0] wdata,
  input  clk,
  input  clr,
  output [31:0] rdata1,
  output [31:0] rdata2
);

  wire demultiplexer_1_out0, demultiplexer_1_out1, demultiplexer_1_out2, demultiplexer_1_out3;
  wire [31:0] demultiplexer_2_out0, demultiplexer_2_out1, demultiplexer_2_out2, demultiplexer_2_out3,
       secreg_1_rdata1, secreg_1_rdata2, secreg_2_rdata1, secreg_2_rdata2, secreg_3_rdata1, secreg_3_rdata2,
       secreg_4_rdata1, secreg_4_rdata2;

  Demultiplexer #(.select(2)) demultiplexer_1 (
    .out0(demultiplexer_1_out0), .out1(demultiplexer_1_out1), .out2(demultiplexer_1_out2),
    .out3(demultiplexer_1_out3), .in(wen), .sel(waddr[4:3]));
  Demultiplexer #(.select(2), .width(32)) demultiplexer_2 (
    .out0(demultiplexer_2_out0), .out1(demultiplexer_2_out1), .out2(demultiplexer_2_out2),
    .out3(demultiplexer_2_out3), .in(wdata), .sel(waddr[4:3]));
  SecReg secreg_1 (
    .raddr1(raddr1[2:0]), .raddr2(raddr2[2:0]), .wen(demultiplexer_1_out0), .waddr(waddr[2:0]),
    .wdata(demultiplexer_2_out0), .clk(clk), .clr(clr), .rdata1(secreg_1_rdata1), .rdata2(secreg_1_rdata2));
  SecReg secreg_2 (
    .raddr1(raddr1[2:0]), .raddr2(raddr2[2:0]), .wen(demultiplexer_1_out1), .waddr(waddr[2:0]),
    .wdata(demultiplexer_2_out1), .clk(clk), .clr(clr), .rdata1(secreg_2_rdata1), .rdata2(secreg_2_rdata2));
  SecReg secreg_3 (
    .raddr1(raddr1[2:0]), .raddr2(raddr2[2:0]), .wen(demultiplexer_1_out2), .waddr(waddr[2:0]),
    .wdata(demultiplexer_2_out2), .clk(clk), .clr(clr), .rdata1(secreg_3_rdata1), .rdata2(secreg_3_rdata2));
  SecReg secreg_4 (
    .raddr1(raddr1[2:0]), .raddr2(raddr2[2:0]), .wen(demultiplexer_1_out3), .waddr(waddr[2:0]),
    .wdata(demultiplexer_2_out3), .clk(clk), .clr(clr), .rdata1(secreg_4_rdata1), .rdata2(secreg_4_rdata2));
  Multiplexer #(.select(2), .width(32)) multiplexer_1 (
    .in0(secreg_1_rdata1), .in1(secreg_2_rdata1), .in2(secreg_3_rdata1), .in3(secreg_4_rdata1), .out(rdata1),
    .sel(raddr1[4:3]));
  Multiplexer #(.select(2), .width(32)) multiplexer_2 (
    .in0(secreg_1_rdata2), .in1(secreg_2_rdata2), .in2(secreg_3_rdata2), .in3(secreg_4_rdata2), .out(rdata2),
    .sel(raddr2[4:3]));
endmodule

module SecReg (
  input  [2:0] raddr1,
  input  [2:0] raddr2,
  input  wen,
  input  [2:0] waddr,
  input  [31:0] wdata,
  input  clk,
  input  clr,
  output [31:0] rdata1,
  output [31:0] rdata2
);

  wire demultiplexer_1_out0, demultiplexer_1_out1, demultiplexer_1_out2, demultiplexer_1_out3,
       demultiplexer_1_out4, demultiplexer_1_out5, demultiplexer_1_out6, demultiplexer_1_out7;
  wire [31:0] demultiplexer_2_out0, demultiplexer_2_out1, demultiplexer_2_out2, demultiplexer_2_out3,
       demultiplexer_2_out4, demultiplexer_2_out5, demultiplexer_2_out6, demultiplexer_2_out7, x0_q, x1_q,
       x2_q, x3_q, x4_q, x5_q, x6_q, x7_q;

  Demultiplexer #(.select(3)) demultiplexer_1 (
    .out0(demultiplexer_1_out0), .out1(demultiplexer_1_out1), .out2(demultiplexer_1_out2),
    .out3(demultiplexer_1_out3), .out4(demultiplexer_1_out4), .out5(demultiplexer_1_out5),
    .out6(demultiplexer_1_out6), .out7(demultiplexer_1_out7), .in(wen), .sel(waddr));
  Demultiplexer #(.select(3), .width(32)) demultiplexer_2 (
    .out0(demultiplexer_2_out0), .out1(demultiplexer_2_out1), .out2(demultiplexer_2_out2),
    .out3(demultiplexer_2_out3), .out4(demultiplexer_2_out4), .out5(demultiplexer_2_out5),
    .out6(demultiplexer_2_out6), .out7(demultiplexer_2_out7), .in(wdata), .sel(waddr));
  Register #(.width(32)) x0 (.D(demultiplexer_2_out0), .en(demultiplexer_1_out0), .clk(clk), .Q(x0_q), .clr(clr));
  Register #(.width(32)) x1 (.D(demultiplexer_2_out1), .en(demultiplexer_1_out1), .clk(clk), .Q(x1_q), .clr(clr));
  Register #(.width(32)) x2 (.D(demultiplexer_2_out2), .en(demultiplexer_1_out2), .clk(clk), .Q(x2_q), .clr(clr));
  Register #(.width(32)) x3 (.D(demultiplexer_2_out3), .en(demultiplexer_1_out3), .clk(clk), .Q(x3_q), .clr(clr));
  Register #(.width(32)) x4 (.D(demultiplexer_2_out4), .en(demultiplexer_1_out4), .clk(clk), .Q(x4_q), .clr(clr));
  Register #(.width(32)) x5 (.D(demultiplexer_2_out5), .en(demultiplexer_1_out5), .clk(clk), .Q(x5_q), .clr(clr));
  Register #(.width(32)) x6 (.D(demultiplexer_2_out6), .en(demultiplexer_1_out6), .clk(clk), .Q(x6_q), .clr(clr));
  Register #(.width(32)) x7 (.D(demultiplexer_2_out7), .en(demultiplexer_1_out7), .clk(clk), .Q(x7_q), .clr(clr));
  Multiplexer #(.select(3), .width(32)) multiplexer_1 (
    .in0(x0_q), .in1(x1_q), .in2(x2_q), .in3(x3_q), .in4(x4_q), .in5(x5_q), .in6(x6_q), .in7(x7_q),
    .out(rdata1), .sel(raddr1));
  Multiplexer #(.select(3), .width(32)) multiplexer_2 (
    .in0(x0_q), .in1(x1_q), .in2(x2_q), .in3(x3_q), .in4(x4_q), .in5(x5_q), .in6(x6_q), .in7(x7_q),
    .out(rdata2), .sel(raddr2));
endmodule

module ALU (
  input  [31:0] alu_source1,
  input  [31:0] alu_source2,
  input  [3:0] alu_control,
  output zero,
  output [31:0] alu_result
);

  wire [31:0] adder_1_out, or_1_out, shifter_1_out, subtractor_1_out;

  Adder #(.width(32)) adder_1 (.a(alu_source1), .b(alu_source2), .out(adder_1_out));  // open: cin, cout
  Subtractor #(.width(32)) subtractor_1 (.a(alu_source1), .b(alu_source2), .out(subtractor_1_out));  // open: bin, bout
  assign or_1_out = alu_source1 | alu_source2;  // OR_Gate or_1, 32 bits wide
  Shifter #(.width(32)) shifter_1 (.in(alu_source2), .\dist (5'b10000), .out(shifter_1_out));
  Multiplexer #(.select(4), .width(32)) multiplexer_1 (
    .in0(adder_1_out), .in1(subtractor_1_out), .in2(or_1_out), .in3(shifter_1_out), .out(alu_result),
    .sel(alu_control));  // open: in4, in5, in6, in7, in8, in9, in10, in11, in12, in13, in14, in15
  Comparator #(.width(32)) comparator_1 (.a({32{1'b0}}), .b(alu_result), .eq(zero));  // open: gt, lt

  // Notes on the sheet:
  //   0000 加法
  //   0001 减法
  //   0010 按位或
  //   0011 逻辑左移
endmodule

module SignExtend (
  input  [15:0] in_1,
  output [31:0] out_2
);

  Multiplexer #(.width(32)) multiplexer_1 (
    .in0({{16{1'b0}}, in_1}), .in1({{16{1'b1}}, in_1}), .out(out_2), .sel(in_1[15]));
endmodule

module ZeroExtend (
  input  [15:0] in_1,
  output [31:0] out_2
);


  assign out_2 = {{16{1'b0}}, in_1};
endmodule

module PC (
  input  zero,
  input  CLK,
  input  [31:0] in_3,
  output [31:0] out_4
);

  Counter #(.max('hffffffff), .width(32)) counter_1 (
    .clr(zero), .load(1'b1), .clk(CLK), .D(in_3), .Q(out_4));  // open: up, count, carry
endmodule

module jicunqi (
  input  [4:0] raddr1,
  input  [4:0] raddr2,
  input  wen,
  input  [4:0] waddr,
  input  [31:0] wdata,
  input  clk,
  input  clr,
  output [31:0] out_8,
  output [31:0] out_9
);

  FirReg firreg_1 (
    .raddr1(raddr1), .raddr2(raddr2), .wen(wen), .waddr(waddr), .wdata(wdata), .clk(clk), .clr(clr),
    .rdata1(out_8), .rdata2(out_9));
endmodule

module ALUmain (
  input  [31:0] alu_source1,
  input  [31:0] alu_source2,
  input  [3:0] alu_control,
  output zero,
  output [31:0] alu_result
);

  ALU alu_1 (
    .alu_source1(alu_source1), .alu_source2(alu_source2), .alu_control(alu_control), .zero(zero),
    .alu_result(alu_result));
endmodule

module controlMain (
  input  [5:0] in_1,
  input  [5:0] in_2,
  output [2:0] out_3,
  output out_4,
  output out_5,
  output out_6,
  output out_7,
  output out_8,
  output out_9,
  output out_10,
  output out_11,
  output [3:0] out_12
);

  cu cu_1 (
    .opcode(in_1), .ALUop(out_3), .RegDst(out_4), .RegWrite(out_5), .ALUSrc(out_6), .MemRead(out_7),
    .MemWrite(out_8), .MemtoReg(out_9), .SeSZ(out_10), .Branch(out_11));
  alucontrol alucontrol_1 (.ALUop(out_3), .func(in_2), .out_3(out_12));
endmodule

module ALU1 (
  input  [31:0] alu_source2,
  input  [31:0] in_2,
  input  [4:0] alu_control,
  output [31:0] cout,
  output flag
);

  wire bne_1_out_3, sub_1_flag, swlw_1_flag;
  wire [31:0] add_1_out_3, ori_1_cout, sub_1_cout, swlw_1_cout;

  ori ori_1 (.imm(alu_source2), .rs(in_2), .cout(ori_1_cout));
  add add_1 (.in_1(alu_source2), .in_2(in_2), .out_3(add_1_out_3));
  sub sub_1 (.rs(in_2), .rt(alu_source2), .flag(sub_1_flag), .cout(sub_1_cout));
  bne bne_1 (.in_1(alu_source2), .in_2(in_2), .out_3(bne_1_out_3));
  swlw swlw_1 (.base(in_2), .imm(alu_source2), .cout(swlw_1_cout), .flag(swlw_1_flag));
  Multiplexer #(.select(5), .width(32)) multiplexer_1 (
    .in1(ori_1_cout), .in2(add_1_out_3), .in4(sub_1_cout), .in16(swlw_1_cout), .out(cout), .sel(alu_control));  // open: in0, in3, in5, in6, in7, in8, in9, in10, in11, in12, in13, in14, in15, in17, in18, in19, in20, in21, in22, in23, in24, in25, in26, in27, in28, in29, in30, in31
  Multiplexer #(.select(5)) multiplexer_2 (
    .in4(sub_1_flag), .in8(bne_1_out_3), .in16(swlw_1_flag), .out(flag), .sel(alu_control));  // open: in0, in1, in2, in3, in5, in6, in7, in9, in10, in11, in12, in13, in14, in15, in17, in18, in19, in20, in21, in22, in23, in24, in25, in26, in27, in28, in29, in30, in31
endmodule

module ori (
  input  [31:0] imm,
  input  [31:0] rs,
  output [31:0] cout
);

  or or_1 (cout[0], imm[0], rs[0]);
  or or_2 (cout[1], imm[1], rs[1]);
  or or_3 (cout[2], imm[2], rs[2]);
  or or_4 (cout[3], imm[3], rs[3]);
  or or_5 (cout[4], imm[4], rs[4]);
  or or_6 (cout[5], imm[5], rs[5]);
  or or_7 (cout[6], imm[6], rs[6]);
  or or_8 (cout[7], imm[7], rs[7]);
  or or_9 (cout[8], imm[8], rs[8]);
  or or_10 (cout[9], imm[9], rs[9]);
  or or_11 (cout[10], imm[10], rs[10]);
  or or_12 (cout[11], imm[11], rs[11]);
  or or_13 (cout[12], imm[12], rs[12]);
  or or_14 (cout[13], imm[13], rs[13]);
  or or_15 (cout[14], imm[14], rs[14]);
  or or_16 (cout[15], imm[15], rs[15]);

  assign cout[31:16] = rs[31:16];
endmodule

module sub (
  input  [31:0] rs,
  input  [31:0] rt,
  output flag,
  output [31:0] cout
);

  wire and_1_out, and_2_out, not_1_out, not_2_out, not_3_out, or_1_out;

  not not_1 (not_1_out, rt[31]);
  Subtractor #(.width(32)) subtractor_1 (.a(rs), .b(rt), .out(cout));  // open: bin, bout
  and and_1 (and_1_out, not_1_out, rt[31], cout[31]);
  not not_2 (not_2_out, rt[31]);
  and and_2 (and_2_out, rt[31], not_2_out, not_3_out);
  not not_3 (not_3_out, cout[31]);
  or or_1 (or_1_out, and_1_out, and_2_out);
  and and_3 (flag, 1'b1, or_1_out);
endmodule

module swlw (
  input  [31:0] base,
  input  [31:0] imm,
  output [31:0] cout,
  output flag
);

  Adder #(.width(32)) adder_1 (.a(base), .b(imm), .out(cout));  // open: cin, cout
  or or_1 (flag, cout[0], cout[1]);
endmodule

module add (
  input  [31:0] in_1,
  input  [31:0] in_2,
  output [31:0] out_3
);

  Adder #(.width(32)) adder_1 (.a(in_1), .b(in_2), .out(out_3));  // open: cin, cout
endmodule

module bne (
  input  [31:0] in_1,
  input  [31:0] in_2,
  output out_3
);

  Comparator #(.width(32)) comparator_1 (.a(in_1), .b(in_2), .eq(out_3));  // open: gt, lt
endmodule
