// Logisim project de3.3.circ as structural Verilog: 7 circuits, main circuit main
module main (
  input  [31:0] alu_source2,
  input  [31:0] alu_source1,
  input  [4:0] alu_control,
  output [31:0] out_4,
  output out_5
);

  ALU alu_1 (.alu_source2(alu_source2), .in_2(alu_source1), .alu_control(alu_control), .cout(out_4), .flag(out_5));
endmodule

module ALU (
  input  [31:0] alu_source2,
  input  [31:0] in_2,
  input  [4:0] alu_control,
  output [31:0] cout,
  output flag
);

  wire bne_1_out_3, sub_1_flag, swlw_1_flag;
  wire [31:0] add_1_out_3, ori_1_cout, sub_1_cout, swlw_1_cout;

  ori ori_1 (.imm(alu_source2), .rs(in_2), .cout(ori_1_cout));
  add add_1 (.in_1(alu_source2), .in_2(in_2), .out_3(add_1_out_3));
  sub sub_1 (.rs(in_2), .rt(alu_source2), .flag(sub_1_flag), .cout(sub_1_cout));
  bne bne_1 (.in_1(alu_source2), .in_2(in_2), .out_3(bne_1_out_3));
  swlw swlw_1 (.base(in_2), .imm(alu_source2), .cout(swlw_1_cout), .flag(swlw_1_flag));
  Multiplexer #(.select(5), .width(32)) multiplexer_1 (
    .in1(ori_1_cout), .in2(add_1_out_3), .in4(sub_1_cout), .in16(swlw_1_cout), .out(cout), .sel(alu_control));  // open: in0, in3, in5, in6, in7, in8, in9, in10, in11, in12, in13, in14, in15, in17, in18, in19, in20, in21, in22, in23, in24, in25, in26, in27, in28, in29, in30, in31
  Multiplexer #(.select(5)) multiplexer_2 (
    .in4(sub_1_flag), .in8(bne_1_out_3), .in16(swlw_1_flag), .out(flag), .sel(alu_control));  // open: in0, in1, in2, in3, in5, in6, in7, in9, in10, in11, in12, in13, in14, in15, in17, in18, in19, in20, in21, in22, in23, in24, in25, in26, in27, in28, in29, in30, in31
endmodule

module ori (
  input  [31:0] imm,
  input  [31:0] rs,
  output [31:0] cout
);

  or or_1 (cout[0], imm[0], rs[0]);
  or or_2 (cout[1], imm[1], rs[1]);
  or or_3 (cout[2], imm[2], rs[2]);
  or or_4 (cout[3], imm[3], rs[3]);
  or or_5 (cout[4], imm[4], rs[4]);
  or or_6 (cout[5], imm[5], rs[5]);
  or or_7 (cout[6], imm[6], rs[6]);
  or or_8 (cout[7], imm[7], rs[7]);
  or or_9 (cout[8], imm[8], rs[8]);
  or or_10 (cout[9], imm[9], rs[9]);
  or or_11 (cout[10], imm[10], rs[10]);
  or or_12 (cout[11], imm[11], rs[11]);
  or or_13 (cout[12], imm[12], rs[12]);
  or or_14 (cout[13], imm[13], rs[13]);
  or or_15 (cout[14], imm[14], rs[14]);
  or or_16 (cout[15], imm[15], rs[15]);

  assign cout[31:16] = rs[31:16];
endmodule

module sub (
  input  [31:0] rs,
  input  [31:0] rt,
  output flag,
  output [31:0] cout
);

  wire and_1_out, and_2_out, not_1_out, not_2_out, not_3_out, or_1_out;

  not not_1 (not_1_out, rt[31]);
  Subtractor #(.width(32)) subtractor_1 (.a(rs), .b(rt), .out(cout));  // open: bin, bout
  and and_1 (and_1_out, not_1_out, rt[31], cout[31]);
  not not_2 (not_2_out, rt[31]);
  and and_2 (and_2_out, rt[31], not_2_out, not_3_out);
  not not_3 (not_3_out, cout[31]);
  or or_1 (or_1_out, and_1_out, and_2_out);
  and and_3 (flag, 1'b1, or_1_out);
endmodule

module swlw (
  input  [31:0] base,
  input  [31:0] imm,
  output [31:0] cout,
  output flag
);

  Adder #(.width(32)) adder_1 (.a(base), .b(imm), .out(cout));  // open: cin, cout
  or or_1 (flag, cout[0], cout[1]);
endmodule

module add (
  input  [31:0] in_1,
  input  [31:0] in_2,
  output [31:0] out_3
);

  Adder #(.width(32)) adder_1 (.a(in_1), .b(in_2), .out(out_3));  // open: cin, cout
endmodule

module bne (
  input  [31:0] in_1,
  input  [31:0] in_2,
  output out_3
);

  Comparator #(.width(32)) comparator_1 (.a(in_1), .b(in_2), .eq(out_3));  // open: gt, lt
endmodule
