// Logisim project Circuit.circ as structural Verilog: 1 circuit, main circuit main
module main (
  input  KL,
  input  KR,
  input  KB,
  input  KS
);

  wire and_1_out, and_2_out, and_3_out, and_4_out, and_5_out, and_6_out, and_7_out, and_8_out, and_9_out,
       and_10_out, and_11_out, CP_out, DLR0_q, DLR0_qn, DLR1_q, F50_out, not_1_out, not_2_out, or_1_out,
       or_2_out, or_3_out, or_4_out, or_5_out, or_6_out, or_7_out, or_8_out, or_9_out, or_10_out, or_11_out,
       or_12_out, xor_1_out, xor_2_out;

  Clock #(.highDuration(8), .lowDuration(8)) CP (.out(CP_out));
  Clock F50 (.out(F50_out));
  not not_1 (not_1_out, KL);
  not not_2 (not_2_out, KR);
  and and_1 (and_1_out, KL, KR);
  and and_2 (and_2_out, KS, F50_out);
  or or_1 (or_1_out, KL, KR);
  and and_3 (and_3_out, not_1_out, KB);
  and and_4 (and_4_out, KB, not_2_out);
  and and_5 (and_5_out, KB, and_1_out);
  or or_2 (or_2_out, and_5_out, and_2_out);
  and and_6 (and_6_out, or_1_out, DLR1_q);
  and and_7 (and_7_out, DLR0_qn, or_1_out);
  or or_3 (or_3_out, and_3_out, or_2_out);
  or or_4 (or_4_out, and_4_out, or_2_out);
  D_Flip_Flop DLR0 (.D(and_6_out), .clk(CP_out), .Q(DLR0_q), .Qn(DLR0_qn));  // open: preset, reset
  D_Flip_Flop DLR1 (.D(and_7_out), .clk(CP_out), .Q(DLR1_q));  // open: Qn, preset, reset
  and and_8 (and_8_out, KL, DLR0_q);
  and and_9 (and_9_out, KL, DLR1_q);
  and and_10 (and_10_out, KR, DLR0_q);
  and and_11 (and_11_out, KR, DLR1_q);
  xor xor_1 (xor_1_out, and_8_out, and_9_out);
  or or_5 (or_5_out, and_9_out, and_8_out);
  or or_6 (or_6_out, and_10_out, and_11_out);
  xor xor_2 (xor_2_out, and_11_out, and_10_out);
  or or_7 (or_7_out, or_3_out, xor_1_out);
  or or_8 (or_8_out, or_3_out, and_9_out);
  or or_9 (or_9_out, or_3_out, or_5_out);
  or or_10 (or_10_out, or_4_out, or_6_out);
  or or_11 (or_11_out, or_4_out, and_11_out);
  or or_12 (or_12_out, or_4_out, xor_2_out);
  LED L1 (.in(or_7_out));
  LED L2 (.in(or_8_out));
  LED L3 (.in(or_9_out));
  LED R3 (.in(or_10_out));
  LED R2 (.in(or_11_out));
  LED R1 (.in(or_12_out));
endmodule
